# Fritzing sketch fritzing-sketch (saved by Fritzing 0.8.7b)
perfboards: 1

parts:
  S1 = Pushbutton [package="[THT]"]
  R1 = Resistor [tolerance=±5% resistance=10k package=THT]
  Digispark1 = Digispark  # not connected
  J1 = female pin header, 6 pins [form="♀ (female)"]
  J2 = female pin header, 3 pins [form="♀ (female)"]

nets:
  N1: S1.Pin_1, S1.Pin_2, R1.Pin_0, J1.pin4
  N2: S1.Pin_3, S1.Pin_4, J2.pin3
  N3: R1.Pin_1, J2.pin2

custom parts:
  Digispark: The Digispark is an Attiny85 based microcontroller development board similar to the Arduino line, only cheaper, smaller, and a bit less powerful. With a whole host of shields to extend its functionality and the ability to use the familiar Arduino IDE the Digispark is a great way to jump into electronics, or perfect for when an Arduino is too big or too much.
